// Logisim project SP1_COMPUTER.circ as structural Verilog: 25 circuits, main circuit main
module main (
  input  in_1,
  input  in_2,
  input  in_3,
  input  in_4,
  input  in_5,
  input  in_6,
  input  in_7,
  input  in_8,
  input  in_9,
  input  in_10,
  input  in_11,
  input  in_12,
  input  in_13,
  input  in_14,
  input  in_15,
  input  in_16,
  input  in_17
);

  wire controlmatrix_1_cp, controlmatrix_1_ea, controlmatrix_1_ep, controlmatrix_1_eu, controlmatrix_1_nce,
       controlmatrix_1_nei, controlmatrix_1_nla, controlmatrix_1_nlb, controlmatrix_1_nli,
       controlmatrix_1_nlm, controlmatrix_1_nlo, controlmatrix_1_out_7, controlmatrix_1_su,
       powersupply_1_clk, powersupply_1_clr_2, powersupply_1_nclk, powersupply_1_nclr, sap_arc_1_out_31,
       sap_arc_1_out_32, sap_arc_1_out_33, sap_arc_1_out_34, sap_arc_1_out_35, sap_arc_1_out_36,
       sap_arc_1_out_37, sap_arc_1_out_38, sap_arc_1_out_39, sap_arc_1_out_40, sap_arc_1_out_41,
       sap_arc_1_out_42;

  PowerSupply powersupply_1 (
    .nHLT(controlmatrix_1_out_7), .MANUAL(in_15), .STEP(in_16), .CLK(powersupply_1_clk),
    .nCLK(powersupply_1_nclk), .CLR(in_17), .nCLR(powersupply_1_nclr), .CLR_2(powersupply_1_clr_2));
  SAP_ARC sap_arc_1 (
    .in_5(in_9), .in_6(in_10), .in_8(in_11), .in_10(in_12), .in_13(in_13), .out_31(sap_arc_1_out_31),
    .out_32(sap_arc_1_out_32), .out_33(sap_arc_1_out_33), .out_34(sap_arc_1_out_34),
    .in_7(controlmatrix_1_nla), .CLK(powersupply_1_clk), .in_11(controlmatrix_1_ea),
    .in_12(controlmatrix_1_nlm), .in_25(controlmatrix_1_eu), .in_24(controlmatrix_1_su),
    .in_29(controlmatrix_1_nlb), .in_30(controlmatrix_1_nlo), .in_28(controlmatrix_1_nli),
    .in_27(controlmatrix_1_nei), .in_2(controlmatrix_1_cp), .in_1(controlmatrix_1_ep),
    .in_23(controlmatrix_1_nce), .in_22(in_14), .out_42(sap_arc_1_out_42), .out_41(sap_arc_1_out_41),
    .out_40(sap_arc_1_out_40), .out_39(sap_arc_1_out_39), .out_38(sap_arc_1_out_38),
    .out_37(sap_arc_1_out_37), .out_36(sap_arc_1_out_36), .out_35(sap_arc_1_out_35),
    .in_3(powersupply_1_nclk), .in_4(powersupply_1_nclr), .CLR(powersupply_1_clr_2), .in_21(in_8),
    .in_20(in_7), .in_19(in_6), .in_18(in_5), .in_14(in_1), .in_15(in_2), .in_16(in_3), .in_17(in_4));
  ControlMatrix controlmatrix_1 (
    .in_1(powersupply_1_clk), .in_2(powersupply_1_nclr), .out_7(controlmatrix_1_out_7),
    .I4(sap_arc_1_out_34), .I3(sap_arc_1_out_33), .I2(sap_arc_1_out_32), .I1(sap_arc_1_out_31),
    .Cp(controlmatrix_1_cp), .Ep(controlmatrix_1_ep), .nLm(controlmatrix_1_nlm), .nCe(controlmatrix_1_nce),
    .nLi(controlmatrix_1_nli), .nEi(controlmatrix_1_nei), .nLa(controlmatrix_1_nla), .Ea(controlmatrix_1_ea),
    .Su(controlmatrix_1_su), .Eu(controlmatrix_1_eu), .nLb(controlmatrix_1_nlb), .nLo(controlmatrix_1_nlo));
  LED led_1 (.in(sap_arc_1_out_35));
  LED led_2 (.in(sap_arc_1_out_39));
  LED led_3 (.in(sap_arc_1_out_36));
  LED led_4 (.in(sap_arc_1_out_38));
  LED led_5 (.in(sap_arc_1_out_37));
  LED led_6 (.in(sap_arc_1_out_42));
  LED led_7 (.in(sap_arc_1_out_40));
  LED led_8 (.in(sap_arc_1_out_41));
endmodule

module DecoderInstruct (
  input  in_1,
  input  in_2,
  input  in_3,
  input  in_4,
  output out_5,
  output out_6,
  output out_7,
  output out_8,
  output out_9
);

  wire not_1_out, not_2_out, not_3_out, not_4_out;

  not not_1 (not_1_out, in_1);
  not not_2 (not_2_out, in_2);
  not not_3 (not_3_out, in_3);
  not not_4 (not_4_out, in_4);
  and and_1 (out_5, not_4_out, not_3_out, not_2_out, not_1_out);
  and and_2 (out_6, in_4, not_3_out, not_2_out, not_1_out);
  and and_3 (out_7, not_4_out, in_3, not_2_out, not_1_out);
  and and_4 (out_8, in_4, in_3, not_2_out, not_1_out);
  nand nand_1 (out_9, in_4, in_3, in_2, in_1);

  // Notes on the sheet:
  //   LDA
  //   ADD
  //   SUB
  //   OUT
  //   \HLT
endmodule

module DringCounter (
  input  CLK,
  input  nCLR,
  output T1,
  output T2,
  output T3,
  output T4,
  output T5,
  output T6
);

  wire not_1_out, not_2_out, not_3_out, not_4_out, not_5_out, not_6_out, not_7_out, not_8_out, not_9_out,
       not_10_out, not_11_out, not_12_out;

  not not_1 (not_1_out, CLK);
  not not_2 (not_2_out, nCLR);
  D_Flip_Flop d_ff_1 (.clk(not_1_out), .D(T6), .Q(T1), .preset(not_2_out));  // open: Qn, en, reset
  D_Flip_Flop d_ff_2 (.clk(not_3_out), .D(T1), .Q(T2), .reset(not_4_out));  // open: Qn, preset, en
  not not_3 (not_3_out, CLK);
  not not_4 (not_4_out, nCLR);
  not not_5 (not_5_out, CLK);
  D_Flip_Flop d_ff_3 (.clk(not_5_out), .D(T2), .Q(T3), .reset(not_6_out));  // open: Qn, preset, en
  not not_6 (not_6_out, nCLR);
  not not_7 (not_7_out, CLK);
  not not_8 (not_8_out, CLK);
  D_Flip_Flop d_ff_4 (.clk(not_7_out), .D(T3), .Q(T4), .reset(not_9_out));  // open: Qn, preset, en
  not not_9 (not_9_out, nCLR);
  D_Flip_Flop d_ff_5 (.clk(not_8_out), .D(T4), .Q(T5), .reset(not_10_out));  // open: Qn, preset, en
  not not_10 (not_10_out, nCLR);
  D_Flip_Flop d_ff_6 (.clk(not_11_out), .D(T5), .Q(T6), .reset(not_12_out));  // open: Qn, preset, en
  not not_11 (not_11_out, CLK);
  not not_12 (not_12_out, nCLR);
endmodule

module ControlMatrix (
  input  in_1,
  input  in_2,
  input  I4,
  input  I3,
  input  I2,
  input  I1,
  output out_7,
  output Cp,
  output Ep,
  output nLm,
  output nCe,
  output nLi,
  output nEi,
  output nLa,
  output Ea,
  output Su,
  output Eu,
  output nLb,
  output nLo
);

  wire c39_1_out_9, c39_1_out_10, c39_1_out_11, c39_1_out_12, c39_2_out_9, c39_2_out_10, c39_2_out_11,
       c39_2_out_12, c39_3_out_9, c39_3_out_10, c39_3_out_11, c39_3_out_12, c39_4_out_9, c39_4_out_10,
       c39_4_out_11, c39_4_out_12, c43_1_out_7, c43_1_out_8, c46_1_out_6, decoderinstruct_1_out_5,
       decoderinstruct_1_out_6, decoderinstruct_1_out_7, decoderinstruct_1_out_8, dringcounter_1_t3,
       dringcounter_1_t4, dringcounter_1_t5, dringcounter_1_t6, not_1_out, not_2_out;

  DecoderInstruct decoderinstruct_1 (
    .out_5(decoderinstruct_1_out_5), .out_6(decoderinstruct_1_out_6), .out_7(decoderinstruct_1_out_7),
    .out_8(decoderinstruct_1_out_8), .out_9(out_7), .in_1(I4), .in_2(I3), .in_3(I2), .in_4(I1));
  DringCounter dringcounter_1 (
    .CLK(in_1), .nCLR(in_2), .T1(Ep), .T2(Cp), .T3(dringcounter_1_t3), .T4(dringcounter_1_t4),
    .T5(dringcounter_1_t5), .T6(dringcounter_1_t6));
  not not_1 (not_1_out, Ep);
  C39 c39_1 (
    .in_1(decoderinstruct_1_out_5), .in_2(dringcounter_1_t4), .in_3(decoderinstruct_1_out_6),
    .in_4(dringcounter_1_t4), .in_5(decoderinstruct_1_out_7), .in_6(dringcounter_1_t4),
    .in_7(decoderinstruct_1_out_5), .in_8(dringcounter_1_t5), .out_9(c39_1_out_9), .out_10(c39_1_out_10),
    .out_11(c39_1_out_11), .out_12(c39_1_out_12));
  not not_2 (not_2_out, dringcounter_1_t3);
  C44 C44 (
    .in_1(not_1_out), .in_2(c39_1_out_9), .in_3(c39_1_out_10), .in_4(c39_1_out_11), .in_5(not_2_out),
    .in_6(c39_1_out_12), .in_7(c39_2_out_9), .in_8(c39_2_out_10), .out_9(nLm), .out_10(nCe));
  C39 c39_2 (
    .in_1(decoderinstruct_1_out_6), .in_2(dringcounter_1_t5), .in_3(decoderinstruct_1_out_7),
    .in_4(dringcounter_1_t5), .in_5(decoderinstruct_1_out_5), .in_6(dringcounter_1_t4),
    .in_7(decoderinstruct_1_out_6), .in_8(dringcounter_1_t4), .out_9(c39_2_out_9), .out_10(c39_2_out_10),
    .out_11(c39_2_out_11), .out_12(c39_2_out_12));
  not not_3 (nLi, dringcounter_1_t3);
  C45 c45_1 (
    .in_1(c39_2_out_11), .in_2(c39_2_out_12), .in_3(c39_3_out_9), .in_4(c39_3_out_10), .in_5(c39_3_out_11),
    .in_6(c39_3_out_12), .out_7(nEi), .out_8(nLa));
  C39 c39_3 (
    .in_1(decoderinstruct_1_out_7), .in_2(dringcounter_1_t4), .in_3(decoderinstruct_1_out_5),
    .in_4(dringcounter_1_t5), .in_5(decoderinstruct_1_out_6), .in_6(dringcounter_1_t6),
    .in_7(decoderinstruct_1_out_7), .in_8(dringcounter_1_t6), .out_9(c39_3_out_9), .out_10(c39_3_out_10),
    .out_11(c39_3_out_11), .out_12(c39_3_out_12));
  not not_4 (Ea, c39_4_out_9);
  C39 c39_4 (
    .in_1(decoderinstruct_1_out_8), .in_2(dringcounter_1_t4), .in_3(decoderinstruct_1_out_7),
    .in_4(dringcounter_1_t6), .in_5(decoderinstruct_1_out_6), .in_6(dringcounter_1_t6),
    .in_7(decoderinstruct_1_out_7), .in_8(dringcounter_1_t6), .out_9(c39_4_out_9), .out_10(c39_4_out_10),
    .out_11(c39_4_out_11), .out_12(c39_4_out_12));
  not not_5 (Su, c39_4_out_10);
  C46 c46_1 (
    .in_1(c39_4_out_11), .in_2(c39_4_out_12), .in_3(c43_1_out_7), .in_4(c43_1_out_8), .out_5(Eu),
    .out_6(c46_1_out_6));
  not not_6 (nLb, c46_1_out_6);
  C43 c43_1 (
    .in_1(decoderinstruct_1_out_6), .in_2(dringcounter_1_t5), .in_3(decoderinstruct_1_out_7),
    .in_4(dringcounter_1_t5), .in_5(decoderinstruct_1_out_8), .in_6(dringcounter_1_t4), .out_7(c43_1_out_7),
    .out_8(c43_1_out_8), .out_9(nLo));

  // Notes on the sheet:
  //   CONTROL MATRIX
  //   C39
  //   C40
  //   C45
  //   C41
  //   C42
  //   C46
  //   C43
endmodule

module C39 (
  input  in_1,
  input  in_2,
  input  in_3,
  input  in_4,
  input  in_5,
  input  in_6,
  input  in_7,
  input  in_8,
  output out_9,
  output out_10,
  output out_11,
  output out_12
);

  nand nand_1 (out_9, in_1, in_2);
  nand nand_2 (out_10, in_3, in_4);
  nand nand_3 (out_11, in_5, in_6);
  nand nand_4 (out_12, in_7, in_8);
endmodule

module C43 (
  input  in_1,
  input  in_2,
  input  in_3,
  input  in_4,
  input  in_5,
  input  in_6,
  output out_7,
  output out_8,
  output out_9
);

  nand nand_1 (out_8, in_3, in_4);
  nand nand_2 (out_7, in_1, in_2);
  nand nand_3 (out_9, in_5, in_6);
endmodule

module SAP_ARC (
  input  in_1,
  input  in_2,
  input  in_3,
  input  in_4,
  input  in_5,
  input  in_6,
  input  in_7,
  input  in_8,
  input  CLK,
  input  in_10,
  input  in_11,
  input  in_12,
  input  in_13,
  input  in_14,
  input  in_15,
  input  in_16,
  input  in_17,
  input  in_18,
  input  in_19,
  input  in_20,
  input  in_21,
  input  in_22,
  input  in_23,
  input  in_24,
  input  in_25,
  input  CLR,
  input  in_27,
  input  in_28,
  input  in_29,
  input  in_30,
  output out_31,
  output out_32,
  output out_33,
  output out_34,
  output out_35,
  output out_36,
  output out_37,
  output out_38,
  output out_39,
  output out_40,
  output out_41,
  output out_42
);

  wire acommulator_1__1, acommulator_1__2, acommulator_1__3, acommulator_1__4, acommulator_1__5,
       acommulator_1__6, acommulator_1__7, acommulator_1__8, acommulator_1_o1, acommulator_1_o2,
       acommulator_1_o3, acommulator_1_o4, acommulator_1_o5, acommulator_1_o6, acommulator_1_o7,
       acommulator_1_o8, b_register_1__1, b_register_1__2, b_register_1__3, b_register_1__4, b_register_1__5,
       b_register_1__6, b_register_1__7, b_register_1__8, ir_register_1_out_17, ir_register_1_out_18,
       ir_register_1_out_19, ir_register_1_out_20, mar_1_a0_2, mar_1_a1_2, mar_1_a2_2, mar_1_a3_2, PC__1,
       PC__2, PC__3, PC__4, ram_1_out_17, ram_1_out_18, ram_1_out_19, ram_1_out_20, ram_1_out_21,
       ram_1_out_22, ram_1_out_23, ram_1_out_24, ula_1_out_19, ula_1_out_20, ula_1_out_21, ula_1_out_22,
       ula_1_out_23, ula_1_out_24, ula_1_out_25, ula_1_out_26, W_BUS_a1, W_BUS_a2, W_BUS_a3, W_BUS_a4,
       W_BUS_d1_2, W_BUS_d1_3, W_BUS_d1_4, W_BUS_d1_5, W_BUS_d2_2, W_BUS_d3_2, W_BUS_d4_2, W_BUS_d8,
       W_BUS_d8_2, W_BUS_d8_3, W_BUS_i1, W_BUS_i2, W_BUS_i3, W_BUS_i4, W_BUS_out_34, W_BUS_out_35,
       W_BUS_out_36, W_BUS_out_37, W_BUS_out_38, W_BUS_out_40, W_BUS_out_54, W_BUS_out_55, W_BUS_out_56,
       W_BUS_out_57, W_BUS_out_58, W_BUS_out_59, W_BUS_out_62, W_BUS_out_63, W_BUS_out_64, W_BUS_out_65,
       W_BUS_out_66, W_BUS_out_67, W_BUS_out_69, W_BUS_out_70, W_BUS_out_71, W_BUS_out_72, W_BUS_out_73,
       W_BUS_out_74, W_BUS_out_75, W_BUS_out_76;

  IR_REGISTER ir_register_1 (
    .CLR(CLR), .nEi(in_27), .nLm(in_28), .CLK(CLK), .in_1(W_BUS_i4), .in_2(W_BUS_i3), .in_3(W_BUS_i2),
    .in_4(W_BUS_d4_2), .in_5(W_BUS_d3_2), .in_6(W_BUS_d2_2), .in_7(W_BUS_d1_3), .in_8(W_BUS_i1),
    .out_13(out_31), .out_14(out_32), .out_15(out_33), .out_16(out_34), .out_17(ir_register_1_out_17),
    .out_18(ir_register_1_out_18), .out_19(ir_register_1_out_19), .out_20(ir_register_1_out_20));
  ProgramCounter PC (.Cp(in_2), .nCLK(in_3), .nCLR(in_4), .Ep(in_1), ._4(PC__4), ._3(PC__3), ._2(PC__2), ._1(PC__1));
  MAR mar_1 (
    .A0(in_5), .A1(in_6), .A2(in_8), .A3(in_10), .PROG(in_13), .in_5(in_12), .in_6(CLK), .in_1(W_BUS_a4),
    .in_2(W_BUS_a3), .in_3(W_BUS_a2), .in_4(W_BUS_a1), .A3_2(mar_1_a3_2), .A2_2(mar_1_a2_2),
    .A1_2(mar_1_a1_2), .A0_2(mar_1_a0_2));
  RAM ram_1 (
    .in_13(in_22), .in_14(CLK), .out_17(ram_1_out_17), .out_18(ram_1_out_18), .out_19(ram_1_out_19),
    .out_20(ram_1_out_20), .in_5(in_14), .in_6(in_15), .in_7(in_16), .in_8(in_17), .in_1(mar_1_a3_2),
    .in_2(mar_1_a2_2), .in_3(mar_1_a1_2), .in_4(mar_1_a0_2), .in_9(in_18), .in_10(in_19), .in_11(in_20),
    .in_12(in_21), .out_21(ram_1_out_21), .out_22(ram_1_out_22), .out_23(ram_1_out_23),
    .out_24(ram_1_out_24), .prog(in_23), .nCE(in_13));
  W_BUS W_BUS (
    .PC1(PC__1), .PC2(PC__2), .PC3(PC__3), .PC4(PC__4), .A4(W_BUS_a4), .A3(W_BUS_a3), .A2(W_BUS_a2),
    .A1(W_BUS_a1), .D4_2(W_BUS_d4_2), .D3_2(W_BUS_d3_2), .D2_2(W_BUS_d2_2), .D1_3(W_BUS_d1_3),
    .Mo8(ram_1_out_21), .in_19(ram_1_out_22), .in_18(ram_1_out_23), .in_17(ram_1_out_24),
    .in_16(ram_1_out_20), .in_15(ram_1_out_19), .in_14(ram_1_out_18), .Mo1(ram_1_out_17), .I4(W_BUS_i4),
    .I3(W_BUS_i3), .I2(W_BUS_i2), .I1(W_BUS_i1), .out_69(W_BUS_out_69), .out_70(W_BUS_out_70),
    .out_71(W_BUS_out_71), .out_72(W_BUS_out_72), .out_73(W_BUS_out_73), .out_74(W_BUS_out_74),
    .out_75(W_BUS_out_75), .out_76(W_BUS_out_76), .D1(ir_register_1_out_20), .D2(ir_register_1_out_19),
    .D3(ir_register_1_out_18), .D4(ir_register_1_out_17), .D1_2(W_BUS_d1_2), .out_34(W_BUS_out_34),
    .out_35(W_BUS_out_35), .out_36(W_BUS_out_36), .out_37(W_BUS_out_37), .out_38(W_BUS_out_38),
    .D8(W_BUS_d8), .out_40(W_BUS_out_40), .Oa1(acommulator_1_o1), .in_2(acommulator_1_o2),
    .in_3(acommulator_1_o3), .in_4(acommulator_1_o4), .in_5(acommulator_1_o5), .in_6(acommulator_1_o6),
    .Oa8(acommulator_1_o7), .in_8(acommulator_1_o8), .S1(ula_1_out_19), .in_22(ula_1_out_20),
    .in_23(ula_1_out_21), .in_24(ula_1_out_22), .in_25(ula_1_out_23), .in_26(ula_1_out_24),
    .S8(ula_1_out_25), .in_28(ula_1_out_26), .D1_4(W_BUS_d1_4), .out_54(W_BUS_out_54), .out_55(W_BUS_out_55),
    .out_56(W_BUS_out_56), .out_57(W_BUS_out_57), .out_58(W_BUS_out_58), .out_59(W_BUS_out_59),
    .D8_2(W_BUS_d8_2), .D1_5(W_BUS_d1_5), .out_62(W_BUS_out_62), .out_63(W_BUS_out_63),
    .out_64(W_BUS_out_64), .out_65(W_BUS_out_65), .out_66(W_BUS_out_66), .out_67(W_BUS_out_67),
    .D8_3(W_BUS_d8_3));
  LED led_1 (.in(W_BUS_out_70));
  LED led_2 (.in(W_BUS_out_69));
  LED led_3 (.in(W_BUS_out_71));
  LED led_4 (.in(W_BUS_out_74));
  LED led_5 (.in(W_BUS_out_72));
  LED led_6 (.in(W_BUS_out_75));
  LED led_7 (.in(W_BUS_out_73));
  LED led_8 (.in(W_BUS_out_76));
  ULA ula_1 (
    .B4(b_register_1__4), .B3(b_register_1__3), .B2(b_register_1__2), .B1(b_register_1__1),
    .B5(b_register_1__5), .B6(b_register_1__6), .B7(b_register_1__7), .B8(b_register_1__8), .Su(in_24),
    .A1(acommulator_1__1), .A2(acommulator_1__2), .A3(acommulator_1__3), .A4(acommulator_1__4),
    .A8(acommulator_1__8), .A7(acommulator_1__7), .A6(acommulator_1__6), .A5(acommulator_1__5),
    .out_23(ula_1_out_23), .out_24(ula_1_out_24), .out_25(ula_1_out_25), .out_26(ula_1_out_26),
    .out_19(ula_1_out_19), .out_20(ula_1_out_20), .out_21(ula_1_out_21), .out_22(ula_1_out_22), .Eu(in_25));
  B_Register b_register_1 (
    .nLb(in_29), .CLK(CLK), .D8(W_BUS_d8_2), .D7(W_BUS_out_59), .D6(W_BUS_out_58), .D5(W_BUS_out_57),
    .D4(W_BUS_out_56), .D3(W_BUS_out_55), .D2(W_BUS_out_54), .D1(W_BUS_d1_4), ._8(b_register_1__8),
    ._7(b_register_1__7), ._6(b_register_1__6), ._5(b_register_1__5), ._4(b_register_1__4),
    ._3(b_register_1__3), ._2(b_register_1__2), ._1(b_register_1__1));
  Acommulator acommulator_1 (
    .O1(acommulator_1_o1), .O2(acommulator_1_o2), .O3(acommulator_1_o3), .O4(acommulator_1_o4),
    .O5(acommulator_1_o5), .O6(acommulator_1_o6), .O7(acommulator_1_o7), .O8(acommulator_1_o8), .nLm(in_7),
    .CLK(CLK), .Ea(in_11), .D8(W_BUS_out_40), .D7(W_BUS_d8), .D6(W_BUS_out_38), .D5(W_BUS_out_37),
    .D4(W_BUS_out_36), .D3(W_BUS_out_35), .D2(W_BUS_out_34), .D1(W_BUS_d1_2), ._8(acommulator_1__8),
    ._7(acommulator_1__7), ._6(acommulator_1__6), ._5(acommulator_1__5), ._4(acommulator_1__4),
    ._3(acommulator_1__3), ._2(acommulator_1__2), ._1(acommulator_1__1));
  OutPutRegister outputregister_1 (
    .nLo(in_30), .CLK(CLK), .D8(W_BUS_d8_3), .D7(W_BUS_out_67), .D6(W_BUS_out_66), .D5(W_BUS_out_65),
    .D4(W_BUS_out_64), .D3(W_BUS_out_63), .D2(W_BUS_out_62), .D1(W_BUS_d1_5), ._8(out_35), ._7(out_36),
    ._6(out_37), ._5(out_38), ._4(out_39), ._3(out_40), ._2(out_41), ._1(out_42));

  // Notes on the sheet:
  //   MAR
  //   IR
endmodule

module ProgramCounter (
  input  Cp,
  input  nCLK,
  input  nCLR,
  input  Ep,
  output _4,
  output _3,
  output _2,
  output _1
);

  wire j_k_ff_1_q, j_k_ff_2_q, j_k_ff_3_q, j_k_ff_4_q, not_1_out, not_2_out, not_3_out, not_4_out, not_5_out,
       not_6_out, not_7_out, not_8_out;

  J_K_Flip_Flop j_k_ff_1 (.J(Cp), .clk(not_1_out), .K(Cp), .Q(j_k_ff_1_q), .reset(not_2_out));  // open: Qn, preset, en
  not not_1 (not_1_out, nCLK);
  not not_2 (not_2_out, nCLR);
  not not_3 (not_3_out, j_k_ff_1_q);
  assign _1 = Ep ? j_k_ff_1_q : 1'bz;  // Controlled_Buffer controlled_buffer_1
  not not_4 (not_4_out, j_k_ff_2_q);
  J_K_Flip_Flop j_k_ff_2 (.J(Cp), .clk(not_3_out), .K(Cp), .Q(j_k_ff_2_q), .reset(not_5_out));  // open: Qn, preset, en
  not not_5 (not_5_out, nCLR);
  assign _2 = Ep ? j_k_ff_2_q : 1'bz;  // Controlled_Buffer controlled_buffer_2
  J_K_Flip_Flop j_k_ff_3 (.J(Cp), .clk(not_4_out), .K(Cp), .Q(j_k_ff_3_q), .reset(not_6_out));  // open: Qn, preset, en
  not not_6 (not_6_out, nCLR);
  assign _3 = Ep ? j_k_ff_3_q : 1'bz;  // Controlled_Buffer controlled_buffer_3
  not not_7 (not_7_out, j_k_ff_3_q);
  not not_8 (not_8_out, nCLR);
  J_K_Flip_Flop j_k_ff_4 (.J(Cp), .clk(not_7_out), .K(Cp), .Q(j_k_ff_4_q), .reset(not_8_out));  // open: Qn, preset, en
  assign _4 = Ep ? j_k_ff_4_q : 1'bz;  // Controlled_Buffer controlled_buffer_4
endmodule

module C44 (
  input  in_1,
  input  in_2,
  input  in_3,
  input  in_4,
  input  in_5,
  input  in_6,
  input  in_7,
  input  in_8,
  output out_9,
  output out_10
);

  wire not_1_out, not_2_out, not_3_out, not_4_out, not_5_out, not_6_out, not_7_out, not_8_out;

  not not_1 (not_1_out, in_1);
  not not_2 (not_2_out, in_2);
  not not_3 (not_3_out, in_3);
  nor nor_1 (out_9, not_1_out, not_2_out, not_3_out, not_4_out);
  not not_4 (not_4_out, in_4);
  not not_5 (not_5_out, in_5);
  not not_6 (not_6_out, in_7);
  not not_7 (not_7_out, in_6);
  not not_8 (not_8_out, in_8);
  nor nor_2 (out_10, not_5_out, not_7_out, not_6_out, not_8_out);
endmodule

module C45 (
  input  in_1,
  input  in_2,
  input  in_3,
  input  in_4,
  input  in_5,
  input  in_6,
  output out_7,
  output out_8
);

  wire not_1_out, not_2_out, not_3_out, not_4_out, not_5_out, not_6_out;

  not not_1 (not_1_out, in_1);
  not not_2 (not_2_out, in_2);
  nor nor_1 (out_7, not_1_out, not_2_out, not_3_out);
  not not_3 (not_3_out, in_3);
  not not_4 (not_4_out, in_4);
  not not_5 (not_5_out, in_5);
  nor nor_2 (out_8, not_4_out, not_5_out, not_6_out);
  not not_6 (not_6_out, in_6);
endmodule

module C46 (
  input  in_1,
  input  in_2,
  input  in_3,
  input  in_4,
  output out_5,
  output out_6
);

  wire not_1_out, not_2_out, not_3_out, not_4_out;

  not not_1 (not_1_out, in_1);
  or or_1 (out_5, not_1_out, not_2_out);
  not not_2 (not_2_out, in_2);
  not not_3 (not_3_out, in_4);
  not not_4 (not_4_out, in_3);
  or or_2 (out_6, not_4_out, not_3_out);
endmodule

module BufferRegister (
  input  X0,
  input  X1,
  input  X2,
  input  X3,
  input  LOAD,
  input  CLK,
  input  CLR,
  input  ENABLE,
  output D0,
  output D1,
  output D2,
  output D3
);

  wire and_1_out, and_2_out, and_3_out, and_4_out, and_5_out, and_6_out, and_7_out, and_8_out, d_ff_1_q,
       d_ff_2_q, d_ff_3_q, d_ff_4_q, not_1_out, or_1_out, or_2_out, or_3_out, or_4_out;

  not not_1 (not_1_out, LOAD);
  and and_1 (and_1_out, LOAD, X0);
  and and_2 (and_2_out, not_1_out, d_ff_1_q);
  or or_1 (or_1_out, and_1_out, and_2_out);
  and and_3 (and_3_out, LOAD, X1);
  or or_2 (or_2_out, and_3_out, and_5_out);
  D_Flip_Flop d_ff_1 (.clk(CLK), .D(or_1_out), .Q(d_ff_1_q), .reset(CLR));  // open: Qn, preset, en
  assign D0 = ENABLE ? d_ff_1_q : 1'bz;  // Controlled_Buffer controlled_buffer_1
  and and_4 (and_4_out, LOAD, X2);
  and and_5 (and_5_out, not_1_out, d_ff_2_q);
  D_Flip_Flop d_ff_2 (.clk(CLK), .D(or_2_out), .Q(d_ff_2_q), .reset(CLR));  // open: Qn, preset, en
  assign D1 = ENABLE ? d_ff_2_q : 1'bz;  // Controlled_Buffer controlled_buffer_2
  and and_6 (and_6_out, not_1_out, d_ff_3_q);
  or or_3 (or_3_out, and_4_out, and_6_out);
  D_Flip_Flop d_ff_3 (.clk(CLK), .D(or_3_out), .Q(d_ff_3_q), .reset(CLR));  // open: Qn, preset, en
  assign D2 = ENABLE ? d_ff_3_q : 1'bz;  // Controlled_Buffer controlled_buffer_3
  and and_7 (and_7_out, LOAD, X3);
  and and_8 (and_8_out, not_1_out, d_ff_4_q);
  or or_4 (or_4_out, and_7_out, and_8_out);
  D_Flip_Flop d_ff_4 (.clk(CLK), .D(or_4_out), .Q(d_ff_4_q), .reset(CLR));  // open: Qn, preset, en
  assign D3 = ENABLE ? d_ff_4_q : 1'bz;  // Controlled_Buffer controlled_buffer_4
endmodule

module MAR (
  input  in_1,
  input  in_2,
  input  in_3,
  input  in_4,
  input  in_5,
  input  in_6,
  input  A0,
  input  A1,
  input  A2,
  input  A3,
  input  PROG,
  output A3_2,
  output A2_2,
  output A1_2,
  output A0_2
);

  wire bufferregister_1_d0, bufferregister_1_d1, bufferregister_1_d2, bufferregister_1_d3,
       n2to1multiplexer_1_out_10, n2to1multiplexer_1_out_11, n2to1multiplexer_1_out_12,
       n2to1multiplexer_1_out_13, not_1_out, not_6_out;

  BufferRegister bufferregister_1 (
    .LOAD(not_6_out), .CLK(in_6), .CLR(not_1_out), .ENABLE(1'b1), .X0(in_4), .X1(in_3), .X2(in_2), .X3(in_1),
    .D0(bufferregister_1_d0), .D1(bufferregister_1_d1), .D2(bufferregister_1_d2), .D3(bufferregister_1_d3));
  not not_1 (not_1_out, 1'b1);
  _2TO1MULTIPLEXER u_2to1multiplexer_1 (
    .in_9(PROG), .in_1(A3), .in_2(bufferregister_1_d3), .in_3(A2), .in_4(bufferregister_1_d2), .in_5(A1),
    .in_6(bufferregister_1_d1), .in_7(A0), .in_8(bufferregister_1_d0), .out_10(n2to1multiplexer_1_out_10),
    .out_11(n2to1multiplexer_1_out_11), .out_12(n2to1multiplexer_1_out_12), .out_13(n2to1multiplexer_1_out_13));
  not not_2 (A3_2, n2to1multiplexer_1_out_10);
  not not_3 (A2_2, n2to1multiplexer_1_out_11);
  not not_4 (A1_2, n2to1multiplexer_1_out_12);
  not not_5 (A0_2, n2to1multiplexer_1_out_13);
  not not_6 (not_6_out, in_5);
endmodule

module _2TO1MULTIPLEXER (
  input  in_1,
  input  in_2,
  input  in_3,
  input  in_4,
  input  in_5,
  input  in_6,
  input  in_7,
  input  in_8,
  input  in_9,
  output out_10,
  output out_11,
  output out_12,
  output out_13
);

  wire and_1_out, and_2_out, and_3_out, and_4_out, and_5_out, and_6_out, and_7_out, and_8_out, and_9_out,
       and_10_out, not_1_out, not_2_out, not_3_out, not_4_out, not_5_out;

  not not_1 (not_1_out, in_9);
  not not_2 (not_2_out, not_1_out);
  and and_1 (and_1_out, not_2_out, not_4_out);
  not not_3 (not_3_out, in_9);
  not not_4 (not_4_out, 1'b0);
  not not_5 (not_5_out, 1'b0);
  and and_2 (and_2_out, not_3_out, not_5_out);
  and and_3 (and_3_out, and_1_out, in_1);
  nor nor_1 (out_10, and_3_out, and_5_out);
  and and_4 (and_4_out, and_1_out, in_3);
  and and_5 (and_5_out, and_2_out, in_2);
  and and_6 (and_6_out, and_2_out, in_4);
  nor nor_2 (out_11, and_4_out, and_6_out);
  and and_7 (and_7_out, and_1_out, in_5);
  nor nor_3 (out_12, and_7_out, and_9_out);
  and and_8 (and_8_out, and_1_out, in_7);
  and and_9 (and_9_out, and_2_out, in_6);
  and and_10 (and_10_out, and_2_out, in_8);
  nor nor_4 (out_13, and_8_out, and_10_out);
endmodule

module IR_REGISTER (
  input  in_1,
  input  in_2,
  input  in_3,
  input  in_4,
  input  in_5,
  input  in_6,
  input  in_7,
  input  in_8,
  input  nLm,
  input  CLR,
  input  nEi,
  input  CLK,
  output out_13,
  output out_14,
  output out_15,
  output out_16,
  output out_17,
  output out_18,
  output out_19,
  output out_20
);

  wire not_1_out, not_2_out, not_3_out;

  BufferRegister bufferregister_1 (
    .LOAD(not_1_out), .CLK(CLK), .CLR(CLR), .ENABLE(1'b1), .X0(in_4), .X1(in_3), .X2(in_2), .X3(in_1),
    .D0(out_16), .D1(out_15), .D2(out_14), .D3(out_13));
  not not_1 (not_1_out, nLm);
  BufferRegister bufferregister_2 (
    .LOAD(not_3_out), .CLK(CLK), .CLR(1'b0), .ENABLE(not_2_out), .X0(in_8), .X1(in_7), .X2(in_6), .X3(in_5),
    .D0(out_20), .D1(out_19), .D2(out_18), .D3(out_17));
  not not_2 (not_2_out, nEi);
  not not_3 (not_3_out, nLm);
endmodule

module W_BUS (
  input  Oa1,
  input  in_2,
  input  in_3,
  input  in_4,
  input  in_5,
  input  in_6,
  input  Oa8,
  input  in_8,
  input  PC1,
  input  PC2,
  input  PC3,
  input  PC4,
  input  Mo1,
  input  in_14,
  input  in_15,
  input  in_16,
  input  in_17,
  input  in_18,
  input  in_19,
  input  Mo8,
  input  S1,
  input  in_22,
  input  in_23,
  input  in_24,
  input  in_25,
  input  in_26,
  input  S8,
  input  in_28,
  input  D1,
  input  D2,
  input  D3,
  input  D4,
  output D1_2,
  output out_34,
  output out_35,
  output out_36,
  output out_37,
  output out_38,
  output D8,
  output out_40,
  output A4,
  output A3,
  output A2,
  output A1,
  output I4,
  output I3,
  output I2,
  output I1,
  output D4_2,
  output D3_2,
  output D2_2,
  output D1_3,
  output D1_4,
  output out_54,
  output out_55,
  output out_56,
  output out_57,
  output out_58,
  output out_59,
  output D8_2,
  output D1_5,
  output out_62,
  output out_63,
  output out_64,
  output out_65,
  output out_66,
  output out_67,
  output D8_3,
  output out_69,
  output out_70,
  output out_71,
  output out_72,
  output out_73,
  output out_74,
  output out_75,
  output out_76
);


  assign A1 = D1;
  assign A2 = D2;
  assign A3 = D3;
  assign A4 = D4;
  assign D1_2 = D1;
  assign D1_3 = D1;
  assign D1_4 = D1;
  assign D1_5 = D1;
  assign D2_2 = D2;
  assign D3_2 = D3;
  assign D4_2 = D4;
  assign D8 = in_19;
  assign D8_2 = in_8;
  assign D8_3 = in_8;
  assign I1 = in_5;
  assign I2 = in_6;
  assign I3 = in_19;
  assign I4 = in_8;
  assign in_2 = D2;
  assign in_3 = D3;
  assign in_4 = D4;
  assign in_14 = D2;
  assign in_15 = D3;
  assign in_16 = D4;
  assign in_17 = in_5;
  assign in_18 = in_6;
  assign in_22 = in_19;
  assign in_23 = in_6;
  assign in_24 = in_5;
  assign in_25 = D4;
  assign in_26 = D3;
  assign in_28 = D1;
  assign Mo1 = D1;
  assign Mo8 = in_8;
  assign Oa1 = D1;
  assign Oa8 = in_19;
  assign out_34 = D2;
  assign out_35 = D3;
  assign out_36 = D4;
  assign out_37 = in_5;
  assign out_38 = in_6;
  assign out_40 = in_8;
  assign out_54 = D2;
  assign out_55 = D3;
  assign out_56 = D4;
  assign out_57 = in_5;
  assign out_58 = in_6;
  assign out_59 = in_19;
  assign out_62 = D2;
  assign out_63 = D3;
  assign out_64 = D4;
  assign out_65 = in_5;
  assign out_66 = in_6;
  assign out_67 = in_19;
  assign out_69 = in_8;
  assign out_70 = in_19;
  assign out_71 = in_6;
  assign out_72 = in_5;
  assign out_73 = D4;
  assign out_74 = D3;
  assign out_75 = D2;
  assign out_76 = D1;
  assign PC1 = D1;
  assign PC2 = D2;
  assign PC3 = D3;
  assign PC4 = D4;
  assign S1 = in_8;
  assign S8 = D2;

  // Notes on the sheet:
  //   PC DATA
endmodule

module RAM_MEMORY (
  input  in_1,
  input  in_2,
  input  in_3,
  input  in_4,
  input  in_5,
  input  in_6,
  input  in_7,
  input  in_8,
  input  in_9,
  input  in_10,
  output Do4,
  output Do3,
  output Do2,
  output Do1
);

  wire and_1_out, and_2_out, and_3_out, and_4_out, and_5_out, and_6_out, and_7_out, and_8_out, and_9_out,
       and_10_out, and_11_out, and_12_out, and_13_out, and_14_out, and_15_out, and_16_out, not_1_out,
       not_2_out, not_3_out, not_4_out, ram4bitschunk_1_output, ram4bitschunk_1_output_2,
       ram4bitschunk_1_output_3, ram4bitschunk_1_output_4, ram4bitschunk_2_output, ram4bitschunk_2_output_2,
       ram4bitschunk_2_output_3, ram4bitschunk_2_output_4, ram4bitschunk_3_output, ram4bitschunk_3_output_2,
       ram4bitschunk_3_output_3, ram4bitschunk_3_output_4, ram4bitschunk_4_output, ram4bitschunk_4_output_2,
       ram4bitschunk_4_output_3, ram4bitschunk_4_output_4, ram4bitschunk_5_output, ram4bitschunk_5_output_2,
       ram4bitschunk_5_output_3, ram4bitschunk_5_output_4, ram4bitschunk_6_output, ram4bitschunk_6_output_2,
       ram4bitschunk_6_output_3, ram4bitschunk_6_output_4, ram4bitschunk_7_output, ram4bitschunk_7_output_2,
       ram4bitschunk_7_output_3, ram4bitschunk_7_output_4, ram4bitschunk_8_output, ram4bitschunk_8_output_2,
       ram4bitschunk_8_output_3, ram4bitschunk_8_output_4, ram4bitschunk_9_output, ram4bitschunk_9_output_2,
       ram4bitschunk_9_output_3, ram4bitschunk_9_output_4, ram4bitschunk_10_output,
       ram4bitschunk_10_output_2, ram4bitschunk_10_output_3, ram4bitschunk_10_output_4,
       ram4bitschunk_11_output, ram4bitschunk_11_output_2, ram4bitschunk_11_output_3,
       ram4bitschunk_11_output_4, ram4bitschunk_12_output, ram4bitschunk_12_output_2,
       ram4bitschunk_12_output_3, ram4bitschunk_12_output_4, ram4bitschunk_13_output,
       ram4bitschunk_13_output_2, ram4bitschunk_13_output_3, ram4bitschunk_13_output_4,
       ram4bitschunk_14_output, ram4bitschunk_14_output_2, ram4bitschunk_14_output_3,
       ram4bitschunk_14_output_4, ram4bitschunk_15_output, ram4bitschunk_15_output_2,
       ram4bitschunk_15_output_3, ram4bitschunk_15_output_4, ram4bitschunk_16_output,
       ram4bitschunk_16_output_2, ram4bitschunk_16_output_3, ram4bitschunk_16_output_4;

  not not_1 (not_1_out, in_1);
  not not_2 (not_2_out, in_2);
  not not_3 (not_3_out, in_3);
  not not_4 (not_4_out, in_4);
  and and_1 (and_1_out, not_4_out, not_3_out, not_2_out, not_1_out);
  and and_2 (and_2_out, in_4, not_3_out, not_2_out, not_1_out);
  and and_3 (and_3_out, in_3, not_4_out, not_2_out, not_1_out);
  and and_4 (and_4_out, in_4, in_3, not_2_out, not_1_out);
  and and_5 (and_5_out, not_4_out, not_3_out, in_2, not_1_out);
  and and_6 (and_6_out, in_4, not_3_out, in_2, not_1_out);
  and and_7 (and_7_out, not_4_out, in_3, in_2, not_1_out);
  and and_8 (and_8_out, in_4, in_3, in_2, not_1_out);
  and and_9 (and_9_out, not_4_out, not_3_out, not_2_out, in_1);
  and and_10 (and_10_out, in_4, not_3_out, not_2_out, in_1);
  and and_11 (and_11_out, not_4_out, in_3, not_2_out, in_1);
  and and_12 (and_12_out, in_4, in_3, not_2_out, in_1);
  and and_13 (and_13_out, not_4_out, not_3_out, in_2, in_1);
  and and_14 (and_14_out, in_4, not_3_out, in_2, in_1);
  and and_15 (and_15_out, not_4_out, in_3, in_2, in_1);
  and and_16 (and_16_out, in_4, in_3, in_2, in_1);
  Ram4bitsChunk ram4bitschunk_1 (
    .in_1(and_15_out), .clk(in_10), .\input (in_8), .input_2(in_7), .input_3(in_6), .input_4(in_9),
    .\output (ram4bitschunk_1_output), .output_2(ram4bitschunk_1_output_2),
    .output_3(ram4bitschunk_1_output_3), .output_4(ram4bitschunk_1_output_4), .read_write(in_5));
  Ram4bitsChunk ram4bitschunk_2 (
    .in_1(and_16_out), .clk(in_10), .\input (in_8), .input_2(in_7), .input_3(in_6), .input_4(in_9),
    .\output (ram4bitschunk_2_output), .output_2(ram4bitschunk_2_output_2),
    .output_3(ram4bitschunk_2_output_3), .output_4(ram4bitschunk_2_output_4), .read_write(in_5));
  Ram4bitsChunk ram4bitschunk_3 (
    .in_1(and_1_out), .clk(in_10), .\input (in_8), .input_2(in_7), .input_3(in_6), .input_4(in_9),
    .\output (ram4bitschunk_3_output), .output_2(ram4bitschunk_3_output_2),
    .output_3(ram4bitschunk_3_output_3), .output_4(ram4bitschunk_3_output_4), .read_write(in_5));
  Ram4bitsChunk ram4bitschunk_4 (
    .in_1(and_2_out), .clk(in_10), .\input (in_8), .input_2(in_7), .input_3(in_6), .input_4(in_9),
    .\output (ram4bitschunk_4_output), .output_2(ram4bitschunk_4_output_2),
    .output_3(ram4bitschunk_4_output_3), .output_4(ram4bitschunk_4_output_4), .read_write(in_5));
  Ram4bitsChunk ram4bitschunk_5 (
    .in_1(and_3_out), .clk(in_10), .\input (in_8), .input_2(in_7), .input_3(in_6), .input_4(in_9),
    .\output (ram4bitschunk_5_output), .output_2(ram4bitschunk_5_output_2),
    .output_3(ram4bitschunk_5_output_3), .output_4(ram4bitschunk_5_output_4), .read_write(in_5));
  Ram4bitsChunk ram4bitschunk_6 (
    .in_1(and_4_out), .clk(in_10), .\input (in_8), .input_2(in_7), .input_3(in_6), .input_4(in_9),
    .\output (ram4bitschunk_6_output), .output_2(ram4bitschunk_6_output_2),
    .output_3(ram4bitschunk_6_output_3), .output_4(ram4bitschunk_6_output_4), .read_write(in_5));
  Ram4bitsChunk ram4bitschunk_7 (
    .in_1(and_5_out), .clk(in_10), .\input (in_8), .input_2(in_7), .input_3(in_6), .input_4(in_9),
    .\output (ram4bitschunk_7_output), .output_2(ram4bitschunk_7_output_2),
    .output_3(ram4bitschunk_7_output_3), .output_4(ram4bitschunk_7_output_4), .read_write(in_5));
  Ram4bitsChunk ram4bitschunk_8 (
    .in_1(and_6_out), .clk(in_10), .\input (in_8), .input_2(in_7), .input_3(in_6), .input_4(in_9),
    .\output (ram4bitschunk_8_output), .output_2(ram4bitschunk_8_output_2),
    .output_3(ram4bitschunk_8_output_3), .output_4(ram4bitschunk_8_output_4), .read_write(in_5));
  Ram4bitsChunk ram4bitschunk_9 (
    .in_1(and_7_out), .clk(in_10), .\input (in_8), .input_2(in_7), .input_3(in_6), .input_4(in_9),
    .\output (ram4bitschunk_9_output), .output_2(ram4bitschunk_9_output_2),
    .output_3(ram4bitschunk_9_output_3), .output_4(ram4bitschunk_9_output_4), .read_write(in_5));
  Ram4bitsChunk ram4bitschunk_10 (
    .in_1(and_8_out), .clk(in_10), .\input (in_8), .input_2(in_7), .input_3(in_6), .input_4(in_9),
    .\output (ram4bitschunk_10_output), .output_2(ram4bitschunk_10_output_2),
    .output_3(ram4bitschunk_10_output_3), .output_4(ram4bitschunk_10_output_4), .read_write(in_5));
  Ram4bitsChunk ram4bitschunk_11 (
    .in_1(and_9_out), .clk(in_10), .\input (in_8), .input_2(in_7), .input_3(in_6), .input_4(in_9),
    .\output (ram4bitschunk_11_output), .output_2(ram4bitschunk_11_output_2),
    .output_3(ram4bitschunk_11_output_3), .output_4(ram4bitschunk_11_output_4), .read_write(in_5));
  Ram4bitsChunk ram4bitschunk_12 (
    .in_1(and_10_out), .clk(in_10), .\input (in_8), .input_2(in_7), .input_3(in_6), .input_4(in_9),
    .\output (ram4bitschunk_12_output), .output_2(ram4bitschunk_12_output_2),
    .output_3(ram4bitschunk_12_output_3), .output_4(ram4bitschunk_12_output_4), .read_write(in_5));
  Ram4bitsChunk ram4bitschunk_13 (
    .in_1(and_11_out), .clk(in_10), .\input (in_8), .input_2(in_7), .input_3(in_6), .input_4(in_9),
    .\output (ram4bitschunk_13_output), .output_2(ram4bitschunk_13_output_2),
    .output_3(ram4bitschunk_13_output_3), .output_4(ram4bitschunk_13_output_4), .read_write(in_5));
  Ram4bitsChunk ram4bitschunk_14 (
    .in_1(and_12_out), .clk(in_10), .\input (in_8), .input_2(in_7), .input_3(in_6), .input_4(in_9),
    .\output (ram4bitschunk_14_output), .output_2(ram4bitschunk_14_output_2),
    .output_3(ram4bitschunk_14_output_3), .output_4(ram4bitschunk_14_output_4), .read_write(in_5));
  Ram4bitsChunk ram4bitschunk_15 (
    .in_1(and_13_out), .clk(in_10), .\input (in_8), .input_2(in_7), .input_3(in_6), .input_4(in_9),
    .\output (ram4bitschunk_15_output), .output_2(ram4bitschunk_15_output_2),
    .output_3(ram4bitschunk_15_output_3), .output_4(ram4bitschunk_15_output_4), .read_write(in_5));
  Ram4bitsChunk ram4bitschunk_16 (
    .in_1(and_14_out), .clk(in_10), .\input (in_8), .input_2(in_7), .input_3(in_6), .input_4(in_9),
    .\output (ram4bitschunk_16_output), .output_2(ram4bitschunk_16_output_2),
    .output_3(ram4bitschunk_16_output_3), .output_4(ram4bitschunk_16_output_4), .read_write(in_5));
  or or_1 (Do4, ram4bitschunk_2_output_3, ram4bitschunk_1_output_3, ram4bitschunk_16_output_3, ram4bitschunk_15_output_3, ram4bitschunk_14_output_3, ram4bitschunk_13_output_3, ram4bitschunk_12_output_3, ram4bitschunk_11_output_3, ram4bitschunk_10_output_3, ram4bitschunk_9_output_3, ram4bitschunk_8_output_3, ram4bitschunk_7_output_3, ram4bitschunk_6_output_3, ram4bitschunk_5_output_3, ram4bitschunk_4_output_3, ram4bitschunk_3_output_3);
  or or_2 (Do3, ram4bitschunk_2_output_2, ram4bitschunk_1_output_2, ram4bitschunk_16_output_2, ram4bitschunk_15_output_2, ram4bitschunk_14_output_2, ram4bitschunk_13_output_2, ram4bitschunk_12_output_2, ram4bitschunk_11_output_2, ram4bitschunk_10_output_2, ram4bitschunk_9_output_2, ram4bitschunk_8_output_2, ram4bitschunk_7_output_2, ram4bitschunk_6_output_2, ram4bitschunk_5_output_2, ram4bitschunk_4_output_2, ram4bitschunk_3_output_2);
  or or_3 (Do2, ram4bitschunk_2_output, ram4bitschunk_1_output, ram4bitschunk_16_output, ram4bitschunk_15_output, ram4bitschunk_14_output, ram4bitschunk_13_output, ram4bitschunk_12_output, ram4bitschunk_11_output, ram4bitschunk_10_output, ram4bitschunk_9_output, ram4bitschunk_8_output, ram4bitschunk_7_output, ram4bitschunk_6_output, ram4bitschunk_5_output, ram4bitschunk_4_output, ram4bitschunk_3_output);
  or or_4 (Do1, ram4bitschunk_2_output_4, ram4bitschunk_1_output_4, ram4bitschunk_16_output_4, ram4bitschunk_15_output_4, ram4bitschunk_14_output_4, ram4bitschunk_13_output_4, ram4bitschunk_12_output_4, ram4bitschunk_11_output_4, ram4bitschunk_10_output_4, ram4bitschunk_9_output_4, ram4bitschunk_8_output_4, ram4bitschunk_7_output_4, ram4bitschunk_6_output_4, ram4bitschunk_5_output_4, ram4bitschunk_4_output_4, ram4bitschunk_3_output_4);
endmodule

module Ram4bitsChunk (
  input  in_1,
  input  clk,
  input  \input ,
  input  input_2,
  input  input_3,
  input  input_4,
  input  read_write,
  output \output ,
  output output_2,
  output output_3,
  output output_4
);

  wire and_1_out, and_2_out, and_4_out, and_5_out, and_7_out, and_8_out, and_10_out, and_11_out, not_1_out,
       not_2_out, not_3_out, not_4_out, not_5_out, not_6_out, not_7_out, not_8_out, s_r_ff_1_q, s_r_ff_1_qn,
       s_r_ff_2_q, s_r_ff_2_qn, s_r_ff_3_q, s_r_ff_3_qn, s_r_ff_4_q, s_r_ff_4_qn;

  not not_1 (not_1_out, input_4);
  and and_1 (and_1_out, in_1, input_4, read_write);
  and and_2 (and_2_out, in_1, not_1_out, read_write);
  S_R_Flip_Flop s_r_ff_1 (
    .S(and_1_out), .clk(clk), .R(and_2_out), .Q(s_r_ff_1_q), .Qn(s_r_ff_1_qn), .preset(1'b0), .reset(1'b0),
    .en(1'b1));
  not not_2 (not_2_out, read_write);
  and and_3 (output_4, in_1, s_r_ff_1_q, not_2_out);
  not not_3 (not_3_out, \input );
  and and_4 (and_4_out, in_1, \input , read_write);
  and and_5 (and_5_out, in_1, not_3_out, read_write);
  S_R_Flip_Flop s_r_ff_2 (
    .S(and_4_out), .clk(clk), .R(and_5_out), .Q(s_r_ff_2_q), .Qn(s_r_ff_2_qn), .preset(1'b0), .reset(1'b0),
    .en(1'b1));
  not not_4 (not_4_out, read_write);
  and and_6 (\output , in_1, s_r_ff_2_q, not_4_out);
  not not_5 (not_5_out, input_2);
  and and_7 (and_7_out, in_1, input_2, read_write);
  and and_8 (and_8_out, in_1, not_5_out, read_write);
  S_R_Flip_Flop s_r_ff_3 (
    .S(and_7_out), .clk(clk), .R(and_8_out), .Q(s_r_ff_3_q), .Qn(s_r_ff_3_qn), .preset(1'b0), .reset(1'b0),
    .en(1'b1));
  not not_6 (not_6_out, read_write);
  and and_9 (output_2, in_1, s_r_ff_3_q, not_6_out);
  not not_7 (not_7_out, input_3);
  and and_10 (and_10_out, in_1, input_3, read_write);
  and and_11 (and_11_out, in_1, not_7_out, read_write);
  S_R_Flip_Flop s_r_ff_4 (
    .S(and_10_out), .clk(clk), .R(and_11_out), .Q(s_r_ff_4_q), .Qn(s_r_ff_4_qn), .preset(1'b0), .reset(1'b0),
    .en(1'b1));
  not not_8 (not_8_out, read_write);
  and and_12 (output_3, in_1, s_r_ff_4_q, not_8_out);
  // also tied to GND on the sheet: {s_r_ff_1_qn, s_r_ff_2_qn, s_r_ff_3_qn, s_r_ff_4_qn}

  // Notes on the sheet:
  //   clk
  //   select
  //   select
  //   read/write
  //   select
  //   read/write
  //   select
  //   read/write
endmodule

module RAM (
  input  in_1,
  input  in_2,
  input  in_3,
  input  in_4,
  input  in_5,
  input  in_6,
  input  in_7,
  input  in_8,
  input  in_9,
  input  in_10,
  input  in_11,
  input  in_12,
  input  in_13,
  input  in_14,
  input  prog,
  input  nCE,
  output out_17,
  output out_18,
  output out_19,
  output out_20,
  output out_21,
  output out_22,
  output out_23,
  output out_24
);

  wire and_1_out, not_1_out, not_2_out, ram_memory_1_do1, ram_memory_1_do2, ram_memory_1_do3,
       ram_memory_1_do4, ram_memory_2_do1, ram_memory_2_do2, ram_memory_2_do3, ram_memory_2_do4;

  RAM_MEMORY ram_memory_1 (
    .in_10(in_14), .in_1(in_1), .in_2(in_2), .in_3(in_3), .in_4(in_4), .in_6(in_5), .in_7(in_6), .in_8(in_7),
    .in_9(in_8), .in_5(in_13), .Do4(ram_memory_1_do4), .Do3(ram_memory_1_do3), .Do2(ram_memory_1_do2),
    .Do1(ram_memory_1_do1));
  assign out_22 = not_1_out ? ram_memory_1_do3 : 1'bz;  // Controlled_Buffer controlled_buffer_1
  assign out_21 = not_1_out ? ram_memory_1_do4 : 1'bz;  // Controlled_Buffer controlled_buffer_2
  assign out_24 = not_1_out ? ram_memory_1_do1 : 1'bz;  // Controlled_Buffer controlled_buffer_3
  assign out_23 = not_1_out ? ram_memory_1_do2 : 1'bz;  // Controlled_Buffer controlled_buffer_4
  RAM_MEMORY ram_memory_2 (
    .in_10(in_14), .in_1(in_1), .in_2(in_2), .in_3(in_3), .in_4(in_4), .in_6(in_9), .in_7(in_10),
    .in_8(in_11), .in_9(in_12), .in_5(in_13), .Do4(ram_memory_2_do4), .Do3(ram_memory_2_do3),
    .Do2(ram_memory_2_do2), .Do1(ram_memory_2_do1));
  and and_1 (and_1_out, prog, not_2_out);
  not not_1 (not_1_out, and_1_out);
  assign out_17 = not_1_out ? ram_memory_2_do1 : 1'bz;  // Controlled_Buffer controlled_buffer_5
  assign out_18 = not_1_out ? ram_memory_2_do2 : 1'bz;  // Controlled_Buffer controlled_buffer_6
  assign out_19 = not_1_out ? ram_memory_2_do3 : 1'bz;  // Controlled_Buffer controlled_buffer_7
  assign out_20 = not_1_out ? ram_memory_2_do4 : 1'bz;  // Controlled_Buffer controlled_buffer_8
  not not_2 (not_2_out, nCE);
endmodule

module Acommulator (
  input  D8,
  input  D7,
  input  D6,
  input  D5,
  input  D4,
  input  D3,
  input  D2,
  input  D1,
  input  nLm,
  input  CLK,
  input  Ea,
  output O1,
  output O2,
  output O3,
  output O4,
  output O5,
  output O6,
  output O7,
  output O8,
  output _8,
  output _7,
  output _6,
  output _5,
  output _4,
  output _3,
  output _2,
  output _1
);

  wire not_1_out, not_2_out;

  assign O1 = Ea ? _1 : 1'bz;  // Controlled_Buffer controlled_buffer_1
  assign O2 = Ea ? _2 : 1'bz;  // Controlled_Buffer controlled_buffer_2
  assign O3 = Ea ? _3 : 1'bz;  // Controlled_Buffer controlled_buffer_3
  assign O4 = Ea ? _4 : 1'bz;  // Controlled_Buffer controlled_buffer_4
  assign O5 = Ea ? _5 : 1'bz;  // Controlled_Buffer controlled_buffer_5
  assign O6 = Ea ? _6 : 1'bz;  // Controlled_Buffer controlled_buffer_6
  assign O7 = Ea ? _7 : 1'bz;  // Controlled_Buffer controlled_buffer_7
  assign O8 = Ea ? _8 : 1'bz;  // Controlled_Buffer controlled_buffer_8
  BufferRegister bufferregister_1 (
    .LOAD(not_1_out), .CLK(CLK), .CLR(1'b0), .ENABLE(1'b1), .X0(D5), .X1(D6), .X2(D7), .X3(D8), .D0(_5),
    .D1(_6), .D2(_7), .D3(_8));
  not not_1 (not_1_out, nLm);
  BufferRegister bufferregister_2 (
    .LOAD(not_2_out), .CLK(CLK), .CLR(1'b0), .ENABLE(1'b1), .X0(D1), .X1(D2), .X2(D3), .X3(D4), .D0(_1),
    .D1(_2), .D2(_3), .D3(_4));
  not not_2 (not_2_out, nLm);
endmodule

module ULA (
  input  A8,
  input  A7,
  input  A6,
  input  A5,
  input  A4,
  input  A3,
  input  A2,
  input  A1,
  input  B8,
  input  B7,
  input  B6,
  input  B5,
  input  B4,
  input  B3,
  input  B2,
  input  B1,
  input  Su,
  input  Eu,
  output out_19,
  output out_20,
  output out_21,
  output out_22,
  output out_23,
  output out_24,
  output out_25,
  output out_26
);

  wire adder_subtractor_1_c_out, adder_subtractor_1_s0, adder_subtractor_1_s1, adder_subtractor_1_s2,
       adder_subtractor_1_s3, adder_subtractor_2_c_out, adder_subtractor_2_s0, adder_subtractor_2_s1,
       adder_subtractor_2_s2, adder_subtractor_2_s3, xor_1_out, xor_2_out, xor_3_out, xor_4_out, xor_5_out,
       xor_6_out, xor_7_out, xor_8_out, xor_9_out;

  xor xor_1 (xor_1_out, Su, adder_subtractor_1_c_out);
  xor xor_2 (xor_2_out, B8, Su);
  Adder_subtractor adder_subtractor_1 (
    .C_IN(adder_subtractor_2_c_out), .A_3(A5), .B_3(xor_4_out), .A(A6), .B(xor_3_out), .A_2(A8),
    .B_2(xor_2_out), .A_4(A7), .B_4(xor_5_out), .S0(adder_subtractor_1_s0), .S1(adder_subtractor_1_s1),
    .S2(adder_subtractor_1_s2), .S3(adder_subtractor_1_s3), .C_OUT(adder_subtractor_1_c_out));
  assign out_20 = Eu ? adder_subtractor_1_s2 : 1'bz;  // Controlled_Buffer controlled_buffer_1
  assign out_21 = Eu ? adder_subtractor_1_s1 : 1'bz;  // Controlled_Buffer controlled_buffer_2
  assign out_22 = Eu ? adder_subtractor_1_s0 : 1'bz;  // Controlled_Buffer controlled_buffer_3
  assign out_19 = Eu ? adder_subtractor_1_s3 : 1'bz;  // Controlled_Buffer controlled_buffer_4
  xor xor_3 (xor_3_out, B6, Su);
  xor xor_4 (xor_4_out, B5, Su);
  xor xor_5 (xor_5_out, B7, Su);
  Adder_subtractor adder_subtractor_2 (
    .C_IN(Su), .A_3(A1), .B_3(xor_9_out), .A(A2), .B(xor_8_out), .A_2(A4), .B_2(xor_7_out), .A_4(A3),
    .B_4(xor_6_out), .S0(adder_subtractor_2_s0), .S1(adder_subtractor_2_s1), .S2(adder_subtractor_2_s2),
    .S3(adder_subtractor_2_s3), .C_OUT(adder_subtractor_2_c_out));
  assign out_23 = Eu ? adder_subtractor_2_s3 : 1'bz;  // Controlled_Buffer controlled_buffer_5
  assign out_26 = Eu ? adder_subtractor_2_s0 : 1'bz;  // Controlled_Buffer controlled_buffer_6
  assign out_25 = Eu ? adder_subtractor_2_s1 : 1'bz;  // Controlled_Buffer controlled_buffer_7
  assign out_24 = Eu ? adder_subtractor_2_s2 : 1'bz;  // Controlled_Buffer controlled_buffer_8
  xor xor_6 (xor_6_out, B3, Su);
  xor xor_7 (xor_7_out, B4, Su);
  xor xor_8 (xor_8_out, B2, Su);
  xor xor_9 (xor_9_out, B1, Su);
endmodule

module B_Register (
  input  D8,
  input  D7,
  input  D6,
  input  D5,
  input  D4,
  input  D3,
  input  D2,
  input  D1,
  input  nLb,
  input  CLK,
  output _8,
  output _7,
  output _6,
  output _5,
  output _4,
  output _3,
  output _2,
  output _1
);

  wire not_1_out, not_2_out;

  BufferRegister bufferregister_1 (
    .LOAD(not_1_out), .CLK(CLK), .CLR(1'b0), .ENABLE(1'b1), .X0(D5), .X1(D6), .X2(D7), .X3(D8), .D0(_5),
    .D1(_6), .D2(_7), .D3(_8));
  not not_1 (not_1_out, nLb);
  BufferRegister bufferregister_2 (
    .LOAD(not_2_out), .CLK(CLK), .CLR(1'b0), .ENABLE(1'b1), .X0(D1), .X1(D2), .X2(D3), .X3(D4), .D0(_1),
    .D1(_2), .D2(_3), .D3(_4));
  not not_2 (not_2_out, nLb);
endmodule

module Adder_subtractor (
  input  A,
  input  B,
  input  A_2,
  input  B_2,
  input  A_3,
  input  B_3,
  input  C_IN,
  input  A_4,
  input  B_4,
  output C_OUT,
  output S1,
  output S0,
  output S3,
  output S2
);

  wire and_1_out, and_2_out, and_3_out, and_4_out, and_5_out, and_6_out, and_7_out, and_8_out, and_9_out,
       and_10_out, and_11_out, and_12_out, or_2_out, or_3_out, or_4_out;

  or or_1 (C_OUT, and_1_out, and_2_out, and_3_out);
  and and_1 (and_1_out, A_2, B_2);
  and and_2 (and_2_out, A_2, or_2_out);
  and and_3 (and_3_out, B_2, or_2_out);
  ExactlyOne xor_1 (.out(S3), .in0(A_2), .in1(B_2), .in2(or_2_out));
  or or_2 (or_2_out, and_4_out, and_5_out, and_6_out);
  and and_4 (and_4_out, A_4, B_4);
  and and_5 (and_5_out, A_4, or_3_out);
  and and_6 (and_6_out, B_4, or_3_out);
  ExactlyOne xor_2 (.out(S2), .in0(A_4), .in1(B_4), .in2(or_3_out));
  or or_3 (or_3_out, and_7_out, and_8_out, and_9_out);
  and and_7 (and_7_out, A, B);
  and and_8 (and_8_out, A, or_4_out);
  and and_9 (and_9_out, B, or_4_out);
  ExactlyOne xor_3 (.out(S1), .in0(A), .in1(B), .in2(or_4_out));
  or or_4 (or_4_out, and_10_out, and_11_out, and_12_out);
  ExactlyOne xor_4 (.out(S0), .in0(A_3), .in1(B_3), .in2(C_IN));
  and and_10 (and_10_out, A_3, B_3);
  and and_11 (and_11_out, A_3, C_IN);
  and and_12 (and_12_out, B_3, C_IN);
endmodule

module OutPutRegister (
  input  D8,
  input  D7,
  input  D6,
  input  D5,
  input  D4,
  input  D3,
  input  D2,
  input  D1,
  input  nLo,
  input  CLK,
  output _8,
  output _7,
  output _6,
  output _5,
  output _4,
  output _3,
  output _2,
  output _1
);

  wire not_1_out, not_2_out;

  BufferRegister bufferregister_1 (
    .LOAD(not_1_out), .CLK(CLK), .CLR(1'b0), .ENABLE(1'b1), .X0(D5), .X1(D6), .X2(D7), .X3(D8), .D0(_5),
    .D1(_6), .D2(_7), .D3(_8));
  not not_1 (not_1_out, nLo);
  BufferRegister bufferregister_2 (
    .LOAD(not_2_out), .CLK(CLK), .CLR(1'b0), .ENABLE(1'b1), .X0(D1), .X1(D2), .X2(D3), .X3(D4), .D0(_1),
    .D1(_2), .D2(_3), .D3(_4));
  not not_2 (not_2_out, nLo);
endmodule

module PowerSupply (
  input  STEP,
  input  MANUAL,
  input  nHLT,
  input  CLR,
  output CLK,
  output nCLK,
  output nCLR,
  output CLR_2
);

  wire clock_1_out, j_k_ff_1_q, nand_1_out, nand_2_out, not_2_out, not_3_out, not_4_out, not_5_out,
       not_6_out, not_7_out;

  Clock clock_1 (.out(clock_1_out));
  not not_1 (nCLR, CLR);
  not not_2 (not_2_out, MANUAL);
  J_K_Flip_Flop j_k_ff_1 (
    .J(nHLT), .clk(not_3_out), .K(nHLT), .Q(j_k_ff_1_q), .reset(not_4_out));  // open: Qn, preset, en
  not not_3 (not_3_out, clock_1_out);
  not not_4 (not_4_out, nCLR);
  not not_5 (not_5_out, not_2_out);
  nand nand_1 (nand_1_out, nHLT, STEP, not_5_out);
  nand nand_2 (nand_2_out, not_2_out, j_k_ff_1_q);
  not not_6 (not_6_out, nand_1_out);
  or or_1 (CLK, not_6_out, not_7_out);
  not not_7 (not_7_out, nand_2_out);
  not not_8 (nCLK, CLK);

  assign CLR_2 = CLR;
endmodule
